// Logisim project turnstile-starter.circ as structural Verilog: 1 circuit, main circuit main
module main (
  input  \input ,
  output \output 
);

  wire clock_out, d_ff_1_q, multiplexer_1_out;

  D_Flip_Flop d_ff_1 (.clk(clock_out), .D(\input ), .Q(d_ff_1_q));  // open: Qn, preset, en, reset
  Multiplexer multiplexer_1 (.in0(d_ff_1_q), .in1(\input ), .out(multiplexer_1_out), .sel(\output ));  // open: en
  Clock clock (.out(clock_out));
  D_Flip_Flop state_bit (.clk(clock_out), .D(multiplexer_1_out), .Q(\output ));  // open: Qn, preset, en, reset

  // Notes on the sheet:
  //   next_state_bit
  //   current_state_bit
endmodule
